# Fritzing sketch XTone Rebuild (saved by Fritzing 0.9.10b)
breadboards: 1

parts:
  Part1 = Adafruit Feather RP2040 [part_number="Adafruit #4884"]
  SA = Round Pushbutton
  SB = Round Pushbutton
  SC = Round Pushbutton
  SD = Round Pushbutton
  SE = Round Pushbutton
  SF = Round Pushbutton
  EXP = Rotary Potentiometer (Large) [maximum_resistance=100kΩ knob_status=50% power=0.5W package=THT]
  Part2 = Adafruit MIDI FeatherWing Kit [part_number=ADA4740]

nets:
  N1: Part1.TX, Part2.MIDI_TX
  N2: Part1.RX, Part2.MIDI_RX
  N3: Part1.A0, EXP.wiper
  GND: Part1.GND, SA.leg0, SB.leg0, SC.leg0, SD.leg0, SE.leg0, SF.leg0, EXP.leg1, Part2.GND
  +3V3: Part1.+3V3, EXP.leg2, Part2.3.3V
  N4: Part1.D13, SA.leg1
  N5: Part1.D12, SB.leg1
  N6: Part1.D11, SC.leg1
  N7: Part1.D10, SD.leg1
  N8: Part1.D9, SE.leg1
  N9: Part1.D6, SF.leg1

custom parts:
  Adafruit Feather RP2040: A new chip means a new Feather, and the Raspberry Pi RP2040 is no exception. When we saw this chip we thought "this chip is going to be awesome when we give it the Feather Treatment" and so we did! This Feather features the RP2040, and all niceties you know and love about Feather Measures 2.0" x 0.9" x 0.28" (50.8mm x 22.8mm x 7mm) without headers soldered in Light as a (large?) feather - 5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
  Adafruit MIDI FeatherWing Kit: Turn your Feather into a song-bird with this musically-enabled FeatherWing that adds MIDI input and output jacks to just about any Feather. You get both input and output DIN-5 MIDI jacks, a 3V optically isolator so you can interface with MIDI on 3.3V logic/power microcontrollers, and two blinky indicator LEDs underneath the jacks to help you know when data is sent and received. For those who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
